// Logisim project ALU_starter.circ as structural Verilog: 2 circuits, main circuit main
module main (
  input  [31:0] IN1,
  input  [31:0] IN2,
  input  [2:0] SEL,
  output [31:0] OUT
);

  ALU alu_1 (.Input1(IN1), .Input2(IN2), .Sel(SEL), .Output(OUT));
endmodule

module ALU (
  input  [31:0] Input1,
  input  [31:0] Input2,
  input  [2:0] Sel,
  output [31:0] Output
);

  wire [4:0] bit_extender_1_out;
  wire [31:0] \and , eo, io, rl, rr, sll, sra, srl;

  Bit_Extender #(.in_width(32), .out_width(5)) bit_extender_1 (.in(Input2), .out(bit_extender_1_out));
  assign \and  = Input1 & Input2;  // AND_Gate and_1, 32 bits wide
  assign io = Input1 | Input2;  // OR_Gate or_1, 32 bits wide
  assign eo = Input1 ^ Input2;  // XOR_Gate xor_1, 32 bits wide
  Shifter #(.width(32)) shifter_1 (.in(Input1), .\dist (bit_extender_1_out), .out(sll));
  Shifter #(.width(32), .shift("lr")) shifter_2 (.in(Input1), .\dist (bit_extender_1_out), .out(srl));
  Shifter #(.width(32), .shift("ar")) shifter_3 (.in(Input1), .\dist (bit_extender_1_out), .out(sra));
  Shifter #(.width(32), .shift("rl")) shifter_4 (.in(Input1), .\dist (bit_extender_1_out), .out(rl));
  Shifter #(.width(32), .shift("rr")) shifter_5 (.in(Input1), .\dist (bit_extender_1_out), .out(rr));
  Multiplexer #(.select(3), .width(32)) multiplexer_1 (
    .in0(sll), .in1(srl), .in2(sra), .in3(rl), .in4(rr), .in5(\and ), .in6(io), .in7(eo), .out(Output),
    .sel(Sel));  // open: en
endmodule
