// Logisim project fib15.circ as structural Verilog: 1 circuit, main circuit main
module main (
  output [9:0] out_1
);

  wire clock_1_out, comparator_1_eq, comparator_2_eq;
  wire [3:0] Counter_q;
  wire [9:0] adder_1_out, Fi_1_q, Fi_2_q, multiplexer_1_out;

  Comparator #(.width(10)) comparator_1 (.a(out_1), .b({10{1'b0}}), .eq(comparator_1_eq));  // open: gt, lt
  Multiplexer #(.width(10), .enable("false")) multiplexer_1 (
    .in0(out_1), .in1(10'h1), .out(multiplexer_1_out), .sel(comparator_1_eq));
  Clock clock_1 (.out(clock_1_out));
  Register #(.width(10)) Fi_2 (.D(Fi_1_q), .Q(Fi_2_q), .clk(clock_1_out));  // open: en, clr
  Register #(.width(10)) Fi_1 (.D(multiplexer_1_out), .Q(Fi_1_q), .clk(clock_1_out));  // open: en, clr
  Counter #(.width(4), .max('hf), .ongoal("stay")) Counter (
    .load(1'b0), .count(1'b1), .Q(Counter_q), .clk(clock_1_out));  // open: D, carry, clr
  Adder #(.width(10)) adder_1 (.a(Fi_2_q), .b(Fi_1_q), .out(adder_1_out));  // open: cin, cout
  Comparator #(.width(4)) comparator_2 (.a(4'b1111), .b(Counter_q), .eq(comparator_2_eq));  // open: gt, lt
  Multiplexer #(.width(10), .enable("false")) multiplexer_2 (
    .in0(adder_1_out), .in1(Fi_1_q), .out(out_1), .sel(comparator_2_eq));
  // Probe on out_1
endmodule
