// Logisim project alu.circ as structural Verilog: 1 circuit, main circuit main
module main (
  input  [5:0] Switch__S,
  input  [31:0] X,
  input  [31:0] Y,
  output Signed_Overflow,
  output [31:0] RESULT,
  output Equal
);

  wire adder_1_cout, adder_2_cout, adder_3_cout, adder_4_cout, addover, comparator_2_lt, comparator_3_lt,
       comparator_4_eq, multiplexer_1_out, multiplexer_2_out, subover;
  wire [4:0] bit_extender_1_out, bit_extender_2_out, bit_extender_3_out;
  wire [6:0] bitadder_1_out;
  wire [31:0] add, addu, \and , bitpal, cnto, negator_1_out, \or , sll, slt, sltu, sra, srl, sub, subu;

  Negator #(.width(32)) negator_1 (.in(Y), .out(negator_1_out));
  Comparator #(.width(32)) comparator_1 (.a(X), .b(Y), .eq(Equal));  // open: gt, lt
  // Probe on {Switch__S[5], Switch__S[3:0]}
  Adder #(.width(31)) adder_1 (.a(X[30:0]), .b(Y[30:0]), .cout(adder_1_cout));  // open: out, cin
  Adder #(.width(32)) adder_2 (.a(X), .b(Y), .out(add), .cout(adder_2_cout));  // open: cin
  Adder #(.width(31)) adder_3 (.a(X[30:0]), .b(negator_1_out[30:0]), .cout(adder_3_cout));  // open: out, cin
  Adder #(.width(32)) adder_4 (.a(X), .b(negator_1_out), .out(sub), .cout(adder_4_cout));  // open: cin
  xor xor_1 (addover, adder_1_cout, adder_2_cout);
  xor xor_2 (subover, adder_3_cout, adder_4_cout);
  Bit_Extender #(.in_width(32), .out_width(5)) bit_extender_1 (.in(Y), .out(bit_extender_1_out));
  Bit_Extender #(.in_width(32), .out_width(5)) bit_extender_2 (.in(Y), .out(bit_extender_2_out));
  Bit_Extender #(.in_width(32), .out_width(5)) bit_extender_3 (.in(Y), .out(bit_extender_3_out));
  Adder #(.width(32)) adder_5 (.a(X), .b(Y), .out(addu));  // open: cin, cout
  Subtractor #(.width(32)) subtractor_1 (.a(X), .b(Y), .out(subu));  // open: bin, bout
  assign \and  = X & Y;  // AND_Gate and_1, 32 bits wide
  assign \or  = X | Y;  // OR_Gate or_1, 32 bits wide
  Comparator #(.width(32)) comparator_2 (.a(X), .b(Y), .lt(comparator_2_lt));  // open: gt, eq
  Comparator #(.width(32), .mode("unsigned")) comparator_3 (.a(X), .b(Y), .lt(comparator_3_lt));  // open: gt, eq
  BitAdder #(.width(32)) bitadder_1 (.in0(X), .in1(Y), .out(bitadder_1_out));
  Shifter #(.width(32)) shifter_1 (.in(X), .\dist (bit_extender_1_out), .out(sll));
  Shifter #(.width(32), .shift("lr")) shifter_2 (.in(X), .\dist (bit_extender_2_out), .out(srl));
  Shifter #(.width(32), .shift("ar")) shifter_3 (.in(X), .\dist (bit_extender_3_out), .out(sra));
  Multiplexer #(.enable("false")) multiplexer_1 (
    .in0(1'b0), .in1(comparator_2_lt), .out(multiplexer_1_out), .sel(comparator_2_lt));
  Multiplexer #(.enable("false")) multiplexer_2 (
    .in0(1'b0), .in1(comparator_3_lt), .out(multiplexer_2_out), .sel(comparator_3_lt));
  assign cnto = {{25{1'b0}}, bitadder_1_out};  // Bit_Extender bit_extender_4
  assign slt = {{31{1'b0}}, multiplexer_1_out};  // Bit_Extender bit_extender_5
  assign sltu = {{31{1'b0}}, multiplexer_2_out};  // Bit_Extender bit_extender_6
  Multiplexer #(.select(5), .width(32), .enable("false")) multiplexer_3 (
    .in0(sll), .in2(srl), .in3(sra), .in16(add), .in17(addu), .in18(sub), .in19(subu), .in20(\and ),
    .in21(\or ), .in26(slt), .in27(sltu), .in28(cnto), .in30(bitpal), .out(RESULT),
    .sel({Switch__S[5], Switch__S[3:0]}));  // open: in1, in4, in5, in6, in7, in8, in9, in10, in11, in12, in13, in14, in15, in22, in23, in24, in25, in29, in31
  Comparator #(.width(16)) comparator_4 (
    .a(X[15:0]),
    .b({X[16], X[17], X[18], X[19], X[20], X[21], X[22], X[23], X[24], X[25], X[26], X[27], X[28], X[29], X[30], X[31]}),
    .eq(comparator_4_eq));  // open: gt, lt
  assign bitpal = {{31{1'b0}}, comparator_4_eq};  // Bit_Extender bit_extender_7
  Multiplexer #(.select(5), .enable("false")) multiplexer_4 (
    .in0(1'b0), .in2(1'b0), .in3(1'b0), .in16(addover), .in17(1'b0), .in18(subover), .in19(1'b0),
    .in20(1'b0), .in21(1'b0), .in26(1'b0), .in27(1'b0), .in28(1'b0), .in30(1'b0), .out(Signed_Overflow),
    .sel({Switch__S[5], Switch__S[3:0]}));  // open: in1, in4, in5, in6, in7, in8, in9, in10, in11, in12, in13, in14, in15, in22, in23, in24, in25, in29, in31

  // Other names for the same wires on the sheet: over = Signed_Overflow; s[4:0] = {Switch__S[5], Switch__S[3:0]}

  // Notes on the sheet:
  //   INPUT to your circuit
  //   INPUTS to your circuit
  //   DON'T CHANGE THE INPUTS AND OUTPUTS! IF YOU DO SO, YOU NEED TO MAKE SURE THE PINS ARE IN THE RIGHT PLACES!
  //   OUTPUTS of your circuit
endmodule
