// Logisim project regfile.circ as structural Verilog: 1 circuit, main circuit main
module main (
  input  [1:0] Read_register_1,
  input  [1:0] Read_register_2,
  input  [1:0] write_register,
  input  [31:0] write_data,
  input  clock,
  input  RegWrite,
  output [31:0] t0_Value,
  output [31:0] t1_Value,
  output [31:0] t2_Value,
  output [31:0] t3_Value,
  output [31:0] Read_Data_1,
  output [31:0] Read_Data_2
);

  wire R0, R1, R2, R3, undriven;

  Register #(.width(32)) register_1 (.D(write_data), .en(R0), .Q(t0_Value), .clk(clock));  // open: clr
  Register #(.width(32)) register_2 (.D(write_data), .en(R1), .Q(t1_Value), .clk(clock), .clr(undriven));
  Register #(.width(32)) register_3 (.D(write_data), .en(R1), .Q(t1_Value), .clk(clock), .clr(undriven));
  Register #(.width(32)) register_4 (.D(write_data), .en(R2), .Q(t2_Value), .clk(clock));  // open: clr
  Multiplexer #(.select(2), .width(32), .enable("false")) multiplexer_1 (
    .in0(t0_Value), .in1(t1_Value), .in2(t2_Value), .in3(t3_Value), .out(Read_Data_1), .sel(Read_register_1));
  Multiplexer #(.select(2), .width(32), .enable("false")) multiplexer_2 (
    .in0(t0_Value), .in1(t1_Value), .in2(t2_Value), .in3(t3_Value), .out(Read_Data_2), .sel(Read_register_2));
  Demultiplexer #(.select(2), .enable("false")) demultiplexer_1 (
    .out0(R0), .out1(R1), .out2(R2), .out3(R3), .in(RegWrite), .sel(write_register));
  Register #(.width(32)) register_5 (.D(write_data), .en(R3), .Q(t3_Value), .clk(clock));  // open: clr

  // Other names for the same wires on the sheet: clk = clock; RD1[31:0] = Read_Data_1; RD2[31:0] = Read_Data_2;
  //   Rr1[1:0] = Read_register_1; Rr2[1:0] = Read_register_2; t0[31:0] = t0_Value; t1[31:0] = t1_Value;
  //   t2[31:0] = t2_Value; t3[31:0] = t3_Value; wd[31:0] = write_data; wr[1:0] = write_register

  // Notes on the sheet:
  //   These are INPUTS to the circuit
  //   These are INPUTS to the circuit
  //   DO NOT CHANGE THE LOCATIONS OF THE INPUTS/OUTPUTS! IF YOU DO SO, YOU NEED TO MAKE SURE THE PINS ARE AT THE RIGHT PLACE!
  //   These are OUTPUTS to the circuit
  //   Yet again, the clock is not an actual clock, but an input, one that will be driven from a higher circuit
  //   These are OUTPUTS to the circuit
endmodule
